// Logisim project alu.circ as structural Verilog: 17 circuits, main circuit inc
module inc (
  input  [2:0] x,
  output [2:0] x_1,
  output Carry_flag
);

  additionneur_retenue_3_bits additionneur_retenue_3_bits_1 (
    .retenue(1'b1), .x(x), .x_retenue(x_1), .Retenue_2(Carry_flag));

  // Notes on the sheet:
  //   Incrémentation
endmodule

module dec (
  input  [2:0] x,
  output [2:0] x_1,
  output Carry_flag
);

  wire [2:0] additionneur_retenue_3_bits_1_x_retenue, not_2_out;

  not not_1 (not_2_out[1], x[1]);
  not not_2 (not_2_out[0], x[0]);
  not not_3 (not_2_out[2], x[2]);
  additionneur_retenue_3_bits additionneur_retenue_3_bits_1 (
    .retenue(1'b1), .x(not_2_out), .x_retenue(additionneur_retenue_3_bits_1_x_retenue), .Retenue_2(Carry_flag));
  not not_4 (x_1[1], additionneur_retenue_3_bits_1_x_retenue[1]);
  not not_5 (x_1[0], additionneur_retenue_3_bits_1_x_retenue[0]);
  not not_6 (x_1[2], additionneur_retenue_3_bits_1_x_retenue[2]);

  // Notes on the sheet:
  //   Décrémentation
endmodule

module adc (
  input  Carry_flag,
  input  [2:0] in_2,
  output [2:0] out_3,
  output Carry_flag_2
);

  additionneur_retenue_3_bits additionneur_retenue_3_bits_1 (
    .retenue(Carry_flag), .x(in_2), .x_retenue(out_3), .Retenue_2(Carry_flag_2));

  // Notes on the sheet:
  //   Ajoute la retenue. Peut-être remplacé par ADD et le registre nul
endmodule

module add (
  input  Carry_flag,
  input  [2:0] x,
  input  [2:0] y,
  output [2:0] x_y,
  output Carry_flag_2
);

  \additionneur_3bits_optimisé  \additionneur_3bits_optimisé_1  (
    .retenue(Carry_flag), .x(x), .y(y), .x_y_retenue(x_y), .Retenue_2(Carry_flag_2));

  // Notes on the sheet:
  //   Additionne deux nombres avec la retenue
endmodule

module \not  (
  input  [2:0] x,
  output [2:0] NON_x
);

  not not_1 (NON_x[1], x[1]);
  not not_2 (NON_x[0], x[0]);
  not not_3 (NON_x[2], x[2]);
endmodule

module not_check (
  input  [4:0] in_1,
  output [1:0] out_2
);

  wire [1:0] n5_2_3_1_out_3;

  not not_1 (out_2[0], n5_2_3_1_out_3[0]);
  _5__2_3 u_5_2_3_1 (.in_1(in_1), .out_3(n5_2_3_1_out_3));  // open: out_2
  not not_2 (out_2[1], n5_2_3_1_out_3[1]);
endmodule

module neg (
  input  [2:0] x,
  output [2:0] minus_x
);

  wire [2:0] not_2_out;

  not not_1 (not_2_out[1], x[1]);
  not not_2 (not_2_out[0], x[0]);
  not not_3 (not_2_out[2], x[2]);
  inc inc_1 (.x(not_2_out), .x_1(minus_x));  // open: Carry_flag

  // Notes on the sheet:
  //   Complément à deux
endmodule

module sub (
  input  [2:0] x,
  input  [2:0] y,
  output [2:0] x_y
);

  wire [2:0] neg_1_minus_x;

  neg neg_1 (.x(y), .minus_x(neg_1_minus_x));
  \additionneur_3bits_optimisé  \additionneur_3bits_optimisé_1  (
    .retenue(1'b0), .x(x), .y(neg_1_minus_x), .x_y_retenue(x_y));  // open: Retenue_2

  // Notes on the sheet:
  //   Soustrait un nombre à un autre
endmodule

module test (
  input  [2:0] x,
  output x___0,
  output x__0
);

  wire or_1_out;

  or or_1 (or_1_out, x[0], x[1]);
  nor nor_1 (x__0, or_1_out, x[2]);

  assign x___0 = x[2];

  // Notes on the sheet:
  //   Met à jour les flags de signe et de nullité
endmodule

module cmp (
  input  [2:0] x,
  input  [2:0] y,
  output x___y,
  output x___y_2
);

  wire [2:0] sub_1_x_y;

  sub sub_1 (.x(x), .y(y), .x_y(sub_1_x_y));
  test test_1 (.x(sub_1_x_y), .x___0(x___y), .x__0(x___y_2));

  // Notes on the sheet:
  //   Compare deux nombres (supériorité / égalité)
  //   Longueur: 8
endmodule

module \and  (
  input  [2:0] x,
  input  [2:0] y,
  output [2:0] x_AND_y
);

  and and_1 (x_AND_y[0], x[0], y[0]);
  and and_2 (x_AND_y[1], x[1], y[1]);
  and and_3 (x_AND_y[2], x[2], y[2]);

  // Notes on the sheet:
  //   Et logique entre deux nombres
  //   Longueur: 1
endmodule

module and_check (
  input  [4:0] in_1,
  input  [4:0] in_2,
  output [1:0] out_3
);

  wire [1:0] additionneur_2bits_1_x_y_retenue, additionneur_retenue_2bits_1_x_retenue,
       code_generator_1_out_2, n5_2_3_1_out_3, n5_2_3_2_out_3, not_1_out;
  wire [2:0] n5_2_3_1_out_2, n5_2_3_2_out_2, or_1_out;

  _5__2_3 u_5_2_3_1 (.in_1(in_1), .out_2(n5_2_3_1_out_2), .out_3(n5_2_3_1_out_3));
  _5__2_3 u_5_2_3_2 (.in_1(in_2), .out_2(n5_2_3_2_out_2), .out_3(n5_2_3_2_out_3));
  or or_1 (or_1_out[0], n5_2_3_1_out_2[0], n5_2_3_2_out_2[0]);
  or or_2 (or_1_out[1], n5_2_3_1_out_2[1], n5_2_3_2_out_2[1]);
  or or_3 (or_1_out[2], n5_2_3_1_out_2[2], n5_2_3_2_out_2[2]);
  additionneur_2bits additionneur_2bits_1 (
    .retenue(1'b0), .x(n5_2_3_1_out_3), .y(n5_2_3_2_out_3), .x_y_retenue(additionneur_2bits_1_x_y_retenue));  // open: Retenue_2
  code_generator code_generator_1 (.in_1(or_1_out), .out_2(code_generator_1_out_2));
  additionneur_retenue_2bits additionneur_retenue_2bits_1 (
    .retenue(1'b1), .x(not_1_out), .x_retenue(additionneur_retenue_2bits_1_x_retenue));
  assign not_1_out = ~code_generator_1_out_2;  // NOT_Gate not_1, 2 bits wide
  additionneur_2bits additionneur_2bits_2 (
    .retenue(1'b0), .x(additionneur_2bits_1_x_y_retenue), .y(additionneur_retenue_2bits_1_x_retenue),
    .x_y_retenue(out_3));  // open: Retenue_2
endmodule

module \or  (
  input  [2:0] x,
  input  [2:0] y,
  output [2:0] x_OR_y
);

  or or_1 (x_OR_y[0], x[0], y[0]);
  or or_2 (x_OR_y[1], x[1], y[1]);
  or or_3 (x_OR_y[2], x[2], y[2]);

  // Notes on the sheet:
  //   Ou logique entre deux nombres
  //   Longueur: 1
endmodule

module or_check (
  input  [4:0] in_1,
  input  [4:0] in_2,
  output [1:0] out_3
);

  wire [1:0] additionneur_2bits_1_x_y_retenue, additionneur_retenue_2bits_1_x_retenue,
       code_generator_1_out_2, n5_2_3_1_out_3, n5_2_3_2_out_3, not_1_out;
  wire [2:0] and_1_out, n5_2_3_1_out_2, n5_2_3_2_out_2;

  _5__2_3 u_5_2_3_1 (.in_1(in_1), .out_2(n5_2_3_1_out_2), .out_3(n5_2_3_1_out_3));
  _5__2_3 u_5_2_3_2 (.in_1(in_2), .out_2(n5_2_3_2_out_2), .out_3(n5_2_3_2_out_3));
  and and_1 (and_1_out[0], n5_2_3_1_out_2[0], n5_2_3_2_out_2[0]);
  and and_2 (and_1_out[1], n5_2_3_1_out_2[1], n5_2_3_2_out_2[1]);
  and and_3 (and_1_out[2], n5_2_3_1_out_2[2], n5_2_3_2_out_2[2]);
  additionneur_2bits additionneur_2bits_1 (
    .retenue(1'b0), .x(n5_2_3_1_out_3), .y(n5_2_3_2_out_3), .x_y_retenue(additionneur_2bits_1_x_y_retenue));  // open: Retenue_2
  code_generator code_generator_1 (.in_1(and_1_out), .out_2(code_generator_1_out_2));
  additionneur_retenue_2bits additionneur_retenue_2bits_1 (
    .retenue(1'b1), .x(not_1_out), .x_retenue(additionneur_retenue_2bits_1_x_retenue));
  assign not_1_out = ~code_generator_1_out_2;  // NOT_Gate not_1, 2 bits wide
  additionneur_2bits additionneur_2bits_2 (
    .retenue(1'b0), .x(additionneur_2bits_1_x_y_retenue), .y(additionneur_retenue_2bits_1_x_retenue),
    .x_y_retenue(out_3));  // open: Retenue_2
endmodule

module \xor  (
  input  [2:0] x,
  input  [2:0] y,
  output [2:0] x_XOR_y
);

  xor xor_1 (x_XOR_y[0], x[0], y[0]);
  xor xor_2 (x_XOR_y[1], x[1], y[1]);
  xor xor_3 (x_XOR_y[2], x[2], y[2]);

  // Notes on the sheet:
  //   Xor logique entre deux nombres
  //   Longueur: 1
endmodule

module add_sub (
  input  [2:0] x,
  input  [2:0] y,
  input  sub,
  output [2:0] x_y,
  output Carry_flag
);

  wire [2:0] additionneur_retenue_3_bits_1_x_retenue, xor_1_out;

  \additionneur_3bits_optimisé  \additionneur_3bits_optimisé_1  (
    .retenue(1'b0), .x(x), .y(additionneur_retenue_3_bits_1_x_retenue), .x_y_retenue(x_y),
    .Retenue_2(Carry_flag));
  xor xor_1 (xor_1_out[0], y[0], sub);
  xor xor_2 (xor_1_out[1], sub, y[1]);
  xor xor_3 (xor_1_out[2], y[2], sub);
  additionneur_retenue_3_bits additionneur_retenue_3_bits_1 (
    .retenue(sub), .x(xor_1_out), .x_retenue(additionneur_retenue_3_bits_1_x_retenue));  // open: Retenue_2
endmodule

module test_check (
  input  [2:0] x,
  input  [2:0] y,
  output [2:0] x_OR_y,
  output CHECK_ERROR
);

  wire xor_1_out, xor_2_out;
  wire [1:0] and_check_1_out_3, code_generator_1_out_2, code_generator_2_out_2, code_generator_3_out_2;
  wire [4:0] n2_3_5_1_out_3, n2_3_5_2_out_3;

  code_generator code_generator_1 (.in_1(x), .out_2(code_generator_1_out_2));
  code_generator code_generator_2 (.in_1(y), .out_2(code_generator_2_out_2));
  \and  and_1 (.x(x), .y(y), .x_AND_y(x_OR_y));
  _2_3__5 u_2_3_5_1 (.in_1(x), .in_2(code_generator_1_out_2), .out_3(n2_3_5_1_out_3));
  _2_3__5 u_2_3_5_2 (.in_1(y), .in_2(code_generator_2_out_2), .out_3(n2_3_5_2_out_3));
  code_generator code_generator_3 (.in_1(x_OR_y), .out_2(code_generator_3_out_2));
  and_check and_check_1 (.in_1(n2_3_5_1_out_3), .in_2(n2_3_5_2_out_3), .out_3(and_check_1_out_3));
  xor xor_1 (xor_1_out, code_generator_3_out_2[0], and_check_1_out_3[0]);
  xor xor_2 (xor_2_out, code_generator_3_out_2[1], and_check_1_out_3[1]);
  or or_1 (CHECK_ERROR, xor_1_out, xor_2_out);

  // Notes on the sheet:
  //   Test manuel uniquement
endmodule
