// Logisim project berger.circ as structural Verilog: 5 circuits, main circuit code_generator
module code_generator (
  input  [2:0] in_1,
  output [1:0] out_2
);

  wire and_1_out, and_2_out, xor_1_out;

  xor xor_1 (xor_1_out, in_1[0], in_1[1]);
  xor xor_2 (out_2[0], xor_1_out, in_1[2]);
  and and_1 (and_1_out, in_1[2], xor_1_out);
  and and_2 (and_2_out, in_1[1], in_1[0]);
  or or_1 (out_2[1], and_1_out, and_2_out);
endmodule

module verificateur (
  input  [4:0] in_1,
  output CHECK_ERROR
);

  wire code_generator_1_p4, code_generator_1_p5, xor_1_out, xor_2_out;

  // code_generator code_generator_1: pin names not known; wires that end beside it: in_1[0], in_1[1], in_1[2], code_generator_1_p4, code_generator_1_p5
  xor xor_1 (xor_1_out, code_generator_1_p5, in_1[4]);
  xor xor_2 (xor_2_out, code_generator_1_p4, in_1[3]);
  or or_1 (CHECK_ERROR, xor_2_out, xor_1_out);

  // Notes on the sheet:
  //   Longueur: 5
endmodule

module allume_si_erreur (
  input  CLK,
  input  [4:0] in_2
);

  wire and_1_out, or_1_out, verificateur_1_check_error;

  verificateur verificateur_1 (.CHECK_ERROR(verificateur_1_check_error), .in_1(in_2));
  and and_1 (and_1_out, CLK, verificateur_1_check_error);
  or or_1 (or_1_out, and_1_out, or_1_out);
  LED led_1 (.in(or_1_out));
endmodule

module _5__2_3 (
  input  [4:0] in_1,
  output [2:0] out_2,
  output [1:0] out_3
);


  assign out_2 = in_1[2:0];
  assign out_3 = in_1[4:3];
endmodule

module _2_3__5 (
  input  [2:0] in_1,
  input  [1:0] in_2,
  output [4:0] out_3
);


  assign out_3 = {in_2, in_1};
endmodule
