// Logisim project controleur_memoire.circ as structural Verilog: 4 circuits, main circuit controleur_memoire
module controleur_memoire (
  input  [4:0] Index_bas,
  input  [4:0] Index_haut,
  input  Avec_index,
  input  [14:0] Adresse,
  input  Lecture,
  input  Ecriture,
  output [4:0] \Entrée_Sortie 
);

  wire or_1_out;
  wire [4:0] transistor_3_out;
  wire [7:7] ram_1_data;
  wire [14:0] additionneur_adresse_1_out_4, transistor_2_out, transistor_4_out;

  additionneur_adresse additionneur_adresse_1 (
    .Index_bas(Index_bas), .Index_haut(Index_haut), .\Adresse_mémoire (Adresse),
    .out_4(additionneur_adresse_1_out_4));  // open: OVERFLOW_ERROR
  Transistor #(.\type ("n"), .width(15)) transistor_1 (
    .in(transistor_2_out), .out(additionneur_adresse_1_out_4), .gate(Avec_index));
  Transistor #(.width(15)) transistor_2 (.in(Adresse), .out(transistor_2_out), .gate(Avec_index));
  Transistor #(.\type ("n"), .width(5)) transistor_3 (.in(\Entrée_Sortie ), .out(transistor_3_out), .gate(or_1_out));
  or or_1 (or_1_out, Lecture, Ecriture);
  Transistor #(.\type ("n"), .width(15)) transistor_4 (.in(transistor_2_out), .out(transistor_4_out), .gate(or_1_out));
  RAM #(.addrWidth(15), .bus("asynch")) ram_1 (
    .addr(transistor_4_out), .data({{3{ram_1_data[7]}}, transistor_3_out}), .ld(Lecture));  // open: sel, clr
  // also tied to GND on the sheet: ram_1_data[7]
endmodule

module additionneur_adresse (
  input  [4:0] Index_bas,
  input  [4:0] Index_haut,
  input  [14:0] \Adresse_mémoire ,
  output [14:0] out_4,
  output OVERFLOW_ERROR
);

  wire additionneur_6bits_1_retenue, and_1_out, and_2_out, and_3_out, and_4_out, and_5_out, and_6_out,
       and_7_out, and_8_out;

  additionneur_6bits additionneur_6bits_1 (
    .x({Index_haut[2:0], Index_bas[2:0]}), .y(\Adresse_mémoire [5:0]), .x_y(out_4[5:0]),
    .retenue(additionneur_6bits_1_retenue));
  xor xor_1 (out_4[6], additionneur_6bits_1_retenue, \Adresse_mémoire [6]);
  and and_1 (and_1_out, additionneur_6bits_1_retenue, \Adresse_mémoire [6]);
  xor xor_2 (out_4[7], and_1_out, \Adresse_mémoire [7]);
  and and_2 (and_2_out, and_1_out, \Adresse_mémoire [7]);
  xor xor_3 (out_4[8], and_2_out, \Adresse_mémoire [8]);
  and and_3 (and_3_out, and_2_out, \Adresse_mémoire [8]);
  xor xor_4 (out_4[9], and_3_out, \Adresse_mémoire [9]);
  and and_4 (and_4_out, and_3_out, \Adresse_mémoire [9]);
  xor xor_5 (out_4[10], and_4_out, \Adresse_mémoire [10]);
  and and_5 (and_5_out, and_4_out, \Adresse_mémoire [10]);
  xor xor_6 (out_4[11], and_5_out, \Adresse_mémoire [11]);
  and and_6 (and_6_out, and_5_out, \Adresse_mémoire [11]);
  xor xor_7 (out_4[12], and_6_out, \Adresse_mémoire [12]);
  and and_7 (and_7_out, and_6_out, \Adresse_mémoire [12]);
  xor xor_8 (out_4[13], and_7_out, \Adresse_mémoire [13]);
  and and_8 (and_8_out, and_7_out, \Adresse_mémoire [13]);
  xor xor_9 (out_4[14], and_8_out, \Adresse_mémoire [14]);
  and and_9 (OVERFLOW_ERROR, and_8_out, \Adresse_mémoire [14]);
endmodule

module additionneur_6bits (
  input  [5:0] x,
  input  [5:0] y,
  output [5:0] x_y,
  output retenue
);

  wire \additionneur_3bits_optimisé_1_p5 ;

  // additionneur_3bits_optimisé additionneur_3bits_optimisé_1: pin names not known; wires that end beside it: 1'b0, x[2:0], y[2:0], x_y[2:0], \additionneur_3bits_optimisé_1_p5 
  // additionneur_3bits_optimisé additionneur_3bits_optimisé_2: pin names not known; wires that end beside it: \additionneur_3bits_optimisé_1_p5 , x[5:3], y[5:3], x_y[5:3], retenue
endmodule

module additionneur_adresse_2 (
  input  [4:0] Index_bas,
  input  [4:0] Index_haut,
  input  [14:0] Adresse,
  output [14:0] Adresse_index,
  output OVERFLOW_ERROR
);

  wire additionneur_6bits_1_retenue, additionneur_retenue_3_bits_1_p4, additionneur_retenue_3_bits_2_p4;

  additionneur_6bits additionneur_6bits_1 (
    .x({Index_haut[2:0], Index_bas[2:0]}), .y(Adresse[5:0]), .x_y(Adresse_index[5:0]),
    .retenue(additionneur_6bits_1_retenue));
  // additionneur_retenue_3_bits additionneur_retenue_3_bits_1: pin names not known; wires that end beside it: additionneur_6bits_1_retenue, Adresse[8:6], Adresse_index[8:6], additionneur_retenue_3_bits_1_p4
  // additionneur_retenue_3_bits additionneur_retenue_3_bits_2: pin names not known; wires that end beside it: additionneur_retenue_3_bits_1_p4, Adresse[11:9], Adresse_index[11:9], additionneur_retenue_3_bits_2_p4
  // additionneur_retenue_3_bits additionneur_retenue_3_bits_3: pin names not known; wires that end beside it: additionneur_retenue_3_bits_2_p4, Adresse[14:12], Adresse_index[14:12], OVERFLOW_ERROR

  // Notes on the sheet:
  //   Strictement équivalent à "aditionneur_adresse
  //   Longueur: 21
endmodule
