// Logisim project register file.circ as structural Verilog: 4 circuits, main circuit bascule_D
module bascule_D (
  input  D,
  input  E,
  output Q
);

  wire and_1_out, and_2_out, nor_2_out, not_1_out;

  not not_1 (not_1_out, D);
  and and_1 (and_1_out, not_1_out, E);
  and and_2 (and_2_out, E, D);
  nor nor_1 (Q, and_1_out, nor_2_out);
  nor nor_2 (nor_2_out, Q, and_2_out);
endmodule

module registre_5b (
  input  Ecriture,
  input  Lecture,
  input  [4:0] in_3,
  output [4:0] out_4
);

  wire bascule_d_1_q, bascule_d_2_q, bascule_d_3_q, bascule_d_4_q, bascule_d_5_q;

  bascule_D bascule_d_1 (.D(in_3[0]), .E(Ecriture), .Q(bascule_d_1_q));
  bascule_D bascule_d_2 (.D(in_3[1]), .E(Ecriture), .Q(bascule_d_2_q));
  bascule_D bascule_d_3 (.D(in_3[2]), .E(Ecriture), .Q(bascule_d_3_q));
  bascule_D bascule_d_4 (.D(in_3[3]), .E(Ecriture), .Q(bascule_d_4_q));
  bascule_D bascule_d_5 (.D(in_3[4]), .E(Ecriture), .Q(bascule_d_5_q));
  Transistor #(.\type ("n")) transistor_1 (.in(bascule_d_1_q), .out(out_4[0]), .gate(Lecture));
  Transistor #(.\type ("n")) transistor_2 (.in(bascule_d_2_q), .out(out_4[1]), .gate(Lecture));
  Transistor #(.\type ("n")) transistor_3 (.in(bascule_d_3_q), .out(out_4[2]), .gate(Lecture));
  Transistor #(.\type ("n")) transistor_4 (.in(bascule_d_4_q), .out(out_4[3]), .gate(Lecture));
  Transistor #(.\type ("n")) transistor_5 (.in(bascule_d_5_q), .out(out_4[4]), .gate(Lecture));
endmodule

module register_file (
  input  Lecture,
  input  Ecriture,
  input  [4:0] \Entrée ,
  input  [2:0] Adresse_Sortie_1,
  input  [2:0] \Adresse_Entrée ,
  input  [2:0] Adresse_Sortie_2,
  output [4:0] Sortie_1,
  output [4:0] Sortie_2,
  output ERROR
);

  wire decoder_1_out0, decoder_1_out1, decoder_1_out2, decoder_1_out3, decoder_1_out4, decoder_1_out5,
       decoder_1_out6, decoder_2_out0, decoder_2_out1, decoder_2_out2, decoder_2_out3, decoder_2_out4,
       decoder_2_out5, decoder_2_out6, decoder_2_out7, decoder_3_out0, decoder_3_out1, decoder_3_out2,
       decoder_3_out3, decoder_3_out4, decoder_3_out5, decoder_3_out6, decoder_3_out7,
       verificateur_1_check_error, verificateur_2_check_error;
  wire [4:0] registre_5b_1_out_4, registre_5b_2_out_4, registre_5b_3_out_4, registre_5b_4_out_4,
       registre_5b_5_out_4, registre_5b_6_out_4, registre_5b_7_out_4, transistor_1_out, transistor_2_out,
       transistor_3_out, transistor_4_out, transistor_5_out, transistor_6_out, transistor_7_out;

  Decoder #(.select(3)) decoder_1 (
    .out0(decoder_1_out0), .out1(decoder_1_out1), .out2(decoder_1_out2), .out3(decoder_1_out3),
    .out4(decoder_1_out4), .out5(decoder_1_out5), .out6(decoder_1_out6), .sel(\Adresse_Entrée ));  // open: out7, en
  Transistor #(.\type ("n"), .width(5)) transistor_1 (.in(\Entrée ), .out(transistor_1_out), .gate(decoder_1_out0));
  Transistor #(.\type ("n"), .width(5)) transistor_2 (.in(\Entrée ), .out(transistor_2_out), .gate(decoder_1_out1));
  Transistor #(.\type ("n"), .width(5)) transistor_3 (.in(\Entrée ), .out(transistor_3_out), .gate(decoder_1_out2));
  Transistor #(.\type ("n"), .width(5)) transistor_4 (.in(\Entrée ), .out(transistor_4_out), .gate(decoder_1_out3));
  Transistor #(.\type ("n"), .width(5)) transistor_5 (.in(\Entrée ), .out(transistor_5_out), .gate(decoder_1_out4));
  Transistor #(.\type ("n"), .width(5)) transistor_6 (.in(\Entrée ), .out(transistor_6_out), .gate(decoder_1_out5));
  Transistor #(.\type ("n"), .width(5)) transistor_7 (.in(\Entrée ), .out(transistor_7_out), .gate(decoder_1_out6));
  registre_5b registre_5b_1 (
    .Ecriture(Ecriture), .Lecture(Lecture), .in_3(transistor_1_out), .out_4(registre_5b_1_out_4));
  registre_5b registre_5b_2 (
    .Ecriture(Ecriture), .Lecture(Lecture), .in_3(transistor_2_out), .out_4(registre_5b_2_out_4));
  registre_5b registre_5b_3 (
    .Ecriture(Ecriture), .Lecture(Lecture), .in_3(transistor_3_out), .out_4(registre_5b_3_out_4));
  registre_5b registre_5b_4 (
    .Ecriture(Ecriture), .Lecture(Lecture), .in_3(transistor_4_out), .out_4(registre_5b_4_out_4));
  registre_5b registre_5b_5 (
    .Ecriture(Ecriture), .Lecture(Lecture), .in_3(transistor_5_out), .out_4(registre_5b_5_out_4));
  registre_5b registre_5b_6 (
    .Ecriture(Ecriture), .Lecture(Lecture), .in_3(transistor_6_out), .out_4(registre_5b_6_out_4));
  registre_5b registre_5b_7 (
    .Ecriture(Ecriture), .Lecture(Lecture), .in_3(transistor_7_out), .out_4(registre_5b_7_out_4));
  Transistor #(.\type ("n"), .width(5)) transistor_8 (.in(registre_5b_1_out_4), .out(Sortie_1), .gate(decoder_2_out0));
  Transistor #(.\type ("n"), .width(5)) transistor_9 (.in(registre_5b_1_out_4), .out(Sortie_2), .gate(decoder_3_out0));
  Transistor #(.\type ("n"), .width(5)) transistor_10 (.in(registre_5b_2_out_4), .out(Sortie_1), .gate(decoder_2_out1));
  Transistor #(.\type ("n"), .width(5)) transistor_11 (.in(registre_5b_2_out_4), .out(Sortie_2), .gate(decoder_3_out1));
  Transistor #(.\type ("n"), .width(5)) transistor_12 (.in(registre_5b_3_out_4), .out(Sortie_1), .gate(decoder_2_out2));
  Transistor #(.\type ("n"), .width(5)) transistor_13 (.in(registre_5b_3_out_4), .out(Sortie_2), .gate(decoder_3_out2));
  Transistor #(.\type ("n"), .width(5)) transistor_14 (.in(registre_5b_4_out_4), .out(Sortie_1), .gate(decoder_2_out3));
  Transistor #(.\type ("n"), .width(5)) transistor_15 (.in(registre_5b_4_out_4), .out(Sortie_2), .gate(decoder_3_out3));
  Transistor #(.\type ("n"), .width(5)) transistor_16 (.in(registre_5b_5_out_4), .out(Sortie_1), .gate(decoder_2_out4));
  Transistor #(.\type ("n"), .width(5)) transistor_17 (.in(registre_5b_5_out_4), .out(Sortie_2), .gate(decoder_3_out4));
  Transistor #(.\type ("n"), .width(5)) transistor_18 (.in(registre_5b_6_out_4), .out(Sortie_1), .gate(decoder_2_out5));
  Transistor #(.\type ("n"), .width(5)) transistor_19 (.in(registre_5b_6_out_4), .out(Sortie_2), .gate(decoder_3_out5));
  Transistor #(.\type ("n"), .width(5)) transistor_20 (.in(registre_5b_7_out_4), .out(Sortie_1), .gate(decoder_2_out6));
  Transistor #(.\type ("n"), .width(5)) transistor_21 (.in(registre_5b_7_out_4), .out(Sortie_2), .gate(decoder_3_out6));
  Transistor #(.\type ("n"), .width(5)) transistor_22 (.in({5{1'b0}}), .out(Sortie_1), .gate(decoder_2_out7));
  Transistor #(.\type ("n"), .width(5)) transistor_23 (.in({5{1'b0}}), .out(Sortie_2), .gate(decoder_3_out7));
  Decoder #(.select(3)) decoder_2 (
    .out0(decoder_2_out0), .out1(decoder_2_out1), .out2(decoder_2_out2), .out3(decoder_2_out3),
    .out4(decoder_2_out4), .out5(decoder_2_out5), .out6(decoder_2_out6), .out7(decoder_2_out7),
    .sel(Adresse_Sortie_1));  // open: en
  verificateur verificateur_1 (.CHECK_ERROR(verificateur_1_check_error), .in_1(Sortie_2));
  Decoder #(.select(3)) decoder_3 (
    .out0(decoder_3_out0), .out1(decoder_3_out1), .out2(decoder_3_out2), .out3(decoder_3_out3),
    .out4(decoder_3_out4), .out5(decoder_3_out5), .out6(decoder_3_out6), .out7(decoder_3_out7),
    .sel(Adresse_Sortie_2));  // open: en
  verificateur verificateur_2 (.CHECK_ERROR(verificateur_2_check_error), .in_1(Sortie_1));
  or or_1 (ERROR, verificateur_2_check_error, verificateur_1_check_error);

  // Notes on the sheet:
  //   Registre nul
endmodule

module registre_5b_reset (
  input  Lecture,
  input  Ecriture,
  input  Reset,
  input  [4:0] in_4,
  output [4:0] out_5
);

  wire not_1_out, or_1_out;
  wire [4:0] and_1_out;

  not not_1 (not_1_out, Reset);
  or or_1 (or_1_out, Ecriture, Reset);
  and and_1 (and_1_out[0], not_1_out, in_4[0]);
  and and_2 (and_1_out[1], not_1_out, in_4[1]);
  and and_3 (and_1_out[2], not_1_out, in_4[2]);
  and and_4 (and_1_out[3], not_1_out, in_4[3]);
  and and_5 (and_1_out[4], not_1_out, in_4[4]);
  registre_5b registre_5b_1 (.Ecriture(or_1_out), .Lecture(Lecture), .in_3(and_1_out), .out_4(out_5));
endmodule
